# Fritzing sketch schema (saved by Fritzing 0.9.2b)
breadboards: 1

parts:
  Parte1 = Arduino Uno (Rev3)
  Parte2 = ENC28J60 Breakout Board
  DHT3 = DHT11 Humitidy and Temperature Sensor
  R4 = Resistor [tolerance=±5% resistance=10k package=THT]

nets:
  N1: Parte1.D8, Parte2.CS
  N2: Parte1.D11_PWM/MOSI, Parte2.SI
  N3: Parte1.D12/MISO, Parte2.SO
  N4: Parte1.D13/SCK, Parte2.SCK
  N5: Parte1.D2, DHT3.DATA, R4.Pin_0
  3V3: Parte1.3V3, Parte2.VCC
  5V: Parte1.5V, DHT3.VDD
  GND: Parte1.GND, Parte2.GND, DHT3.GND, R4.Pin_1

notes:
  ENC28J60 chip:
  VCC 3.3V
  GND GND
  SCK Pin 13
  SO Pin 12
  SI Pin 11
  CS Pin 8

custom parts:
  ENC28J60 Breakout Board: This is a breakout board for the Microchip ENC28J60 stand-alone ethernet controller. The ENC28J60 has an SPI interface. It operates at 3.3 Volts.
  DHT11 Humitidy and Temperature Sensor: DHT11 Humidity and Temperature Sensor
